# Fritzing sketch conecciones robotfzz (saved by Fritzing 0.9.3b)
breadboards: 1

parts:
  Componente1 = Motor Driver 1A Dual TB6612FNG
  Componente2 = Arduino Nano (Rev3.0) (ICSP)
  S1 = Pololu QTR-8 Reflectabce Sensor array [package=THT]
  M1 = DC Motor
  M2 = DC Motor
  VCC1 = 4 x AA Battery Box

nets:
  N1: Componente1.GND, S1.pin15, VCC1.-
  N2: Componente1.B01, M2.pin_1
  N3: Componente1.B02, M2.pin_2
  N4: Componente1.A02, M1.pin_1
  N5: Componente1.A01, M1.pin_2
  N6: Componente1.VCC, Componente1.VM, S1.pin14, S1.pin22, VCC1.+
  N7: Componente1.PWMA, Componente2.D6
  N8: Componente1.AIN2, Componente2.D7
  N9: Componente1.AIN1, Componente2.D8
  N10: Componente1.STBY, Componente2.D5
  N11: Componente1.BIN1, Componente2.D9
  N12: Componente1.BIN2, Componente2.D10
  N13: Componente1.PWMB, Componente2.D11/MOSI
  N14: Componente2.D12/MISO, S1.pin13
  N15: Componente2.A7, S1.pin5
  N16: Componente2.A6, S1.pin6
  N17: Componente2.A5, S1.pin7
  N18: Componente2.A4, S1.pin8
  N19: Componente2.A3, S1.pin9
  N20: Componente2.A2, S1.pin10
  N21: Componente2.A1, S1.pin11
  N22: Componente2.A0, S1.pin12

custom parts:
  4 x AA Battery Box: A 4 x AA battery box.
